# Fritzing sketch ugame-10 (saved by Fritzing 0.9.3b)
circuit board: 4.19999cm x 4.99999cm
breadboards: 1

parts:
  X5 = SWITCH-MOMENTARY-2 [package=tactile-switch-1101ne]
  X6 = SWITCH-MOMENTARY-2 [package=tactile-switch-1101ne]
  X7 = SWITCH-MOMENTARY-2 [package=tactile-switch-1101ne]
  X4 = SWITCH-MOMENTARY-2 [package=tactile-switch-1101ne]
  X9 = SWITCH-MOMENTARY-2 [package=tactile-switch-1101ne]
  X8 = SWITCH-MOMENTARY-2 [package=tactile-switch-1101ne]
  X1 = USB Connectors [package=usb-microb]
  U3 = samd21e [chip_label=IC]
  U1 = AT25FS010 [package=so08wide]
  U6 = st7735-14pin [part_number=ST7735]
  C1 = Ceramic Capacitor [capacitance=1µF package="0603 [SMD, multilayer]"]
  U4 = Voltage Regulator LDO [package=sot23-5]
  C2 = Ceramic Capacitor [capacitance=1µF package="0603 [SMD, multilayer]"]
  D1 = Rectifier Diode [package="Melf DO-213 AA [SMD]"]
  U2 = mcp73831t
  R1 = Resistor [tolerance=±5% resistance=10k package="0402 [SMD]"]
  R2 = Resistor [tolerance=±5% resistance=2k package="0402 [SMD]"]
  R3 = Resistor [tolerance=±5% resistance=2.4k package="0402 [SMD]"]
  CHARGE = smd LED [color="Orange (605nm)" package="0603 [SMD]"]
  R4 = Resistor [tolerance=±5% resistance=300 package="0402 [SMD]"]
  X2 = SPST Switch [package=switch-spst-smd-a]
  Pad5 = Pad [width=7 height=2 connect=center]
  R6 = Resistor [tolerance=±5% resistance=47k package="0402 [SMD]"]
  U5 = PAM8301 [part_number=PAM8301AAF]
  R8 = Resistor [tolerance=±10% resistance=10k package="0402 [SMD]"]
  R7 = Resistor [tolerance=±10% resistance=47k package="0402 [SMD]"]
  C3 = Ceramic Capacitor [capacitance=100nF package="0603 [SMD, multilayer]"]
  SPKR = Pad [width=1.27 height=2.54 connect=center]
  + = Pad [width=1.27 height=2.54 connect=center]
  +_2 = Pad [width=2.6000000000000001 height=3 connect=center]
  SWCLK = Pad [width=2.54 height=2.54 connect=center]
  SWDIO = Pad [width=2.54 height=2.54 connect=center]
  - = Pad [width=2.6000000000000001 height=3 connect=center]
  R5 = Resistor [tolerance=±5% resistance=47k package="0402 [SMD]"]
  RESET = Pad [width=1.27 height=2.54 connect=center]
  X3 = Pad [width=1.27 height=2.54 connect=center]
  GND = Pad [width=2.54 height=2.54 connect=center]
  J1 = female pin header, 4 pins [form="♀ (female)"]
  +_- = female pin header, 2 pins [form="♀ (female)"]
  3V3 = Pad [width=2.54 height=2.54 connect=center]
  nRST = Pad [width=2.54 height=2.54 connect=center]

nets:
  GND: X5.1, X6.2, X7.2, X4.1, X9.2, X8.1, X1.GND, U3.connector9, U3.connector27, U1.GND, U6.connector1, U6.connector2, U6.connector4, U6.connector12, C1.0, U4.GND, C2.0, U2.connector1, R2.Pin_1, Pad5.pad, R6.Pin_0, U5.connector4, -.pad, X3.pad, GND.pad, +_-.pin1
  BUTTON UP: X5.2, U3.connector3
  BUTTON DOWN: X6.1, U3.connector20
  BUTTON RIGHT: X7.1, U3.connector5
  BUTTON LEFT: X4.2, U3.connector4
  BUTTON X: X9.1, U3.connector1
  BUTTON O: X8.2, U3.connector0
  USB D+: X1.D+, U3.connector23
  USB D-: X1.D-, U3.connector22
  N1: X1.VBUS, U4.IN, U4.EN, D1.cathode, U2.connector3, CHARGE.anode
  SPEAKER: U3.connector2, R7.Pin_1
  DISPLAY MOSI: U3.connector6, U6.connector7
  DISPLAY SCK: U3.connector7, U6.connector8
  3.3V: U3.connector8, U3.connector29, U1.WP, U1.HOLD, U1.VCC, U6.connector9, U6.connector10, U4.OUT, C2.1, R1.Pin_1, R4.Pin_0, U5.connector1, R8.Pin_1, 3V3.pad
  DISPLAY CS: U3.connector10, U6.connector11
  DISPLAY D/C: U3.connector11, U6.connector6
  BATTERY: U3.connector12, R6.Pin_1, R5.Pin_0
  A: U3.connector13, J1.pin4
  B: U3.connector14, J1.pin3
  C: U3.connector15, J1.pin2
  FLASH MOSI: U3.connector16, U1.SI
  FLASH SCK: U3.connector17, U1.SCK
  FLASH CS: U3.connector18, U1.CS, R1.Pin_0
  FLASH MISO: U3.connector19, U1.SO
  MUTE: U3.connector21, U5.connector2, R8.Pin_0
  RESET: U3.connector25, U6.connector5, RESET.pad, nRST.pad
  D: U3.connector26, J1.pin1
  N2: U3.connector28, C1.1
  SWDCLK: U3.connector30, SWCLK.pad
  SWDIO: U3.connector31, SWDIO.pad
  N3: U6.connector3, R4.Pin_1
  N4: D1.anode, U2.connector2, X2.O, X2.P, R5.Pin_1
  N5: U2.connector0, R3.Pin_1
  N6: U2.connector4, R2.Pin_0
  N7: R3.Pin_0, CHARGE.cathode
  N8: X2.S, +_2.pad, +_-.pin2
  N9: U5.connector0, +.pad
  N10: U5.connector3, C3.1
  N11: U5.connector5, SPKR.pad
  N12: R7.Pin_0, C3.0

notes:
  http://hackaday.io/project/27629
  A B C D
  o
  x
  .
